# Fritzing sketch wiring-outside-box (saved by Fritzing 0.9.3b)
breadboards: 1

parts:
  WeMos_D1_Mini_v2 = WeMos D1 Mini  # not connected
  DHT22 = DHT22 Humidity and Temperature Sensor
  part = Resistor [tolerance=±5% resistance=10k package=THT]
  part_2 = Resistor [tolerance=±5% resistance=4.7k package=THT]
  part_3 = Resistor [tolerance=±5% resistance=1k package=THT]
  part_4 = Resistor [tolerance=±5% resistance=220 package=THT]
  BMP180 = Adafruit BMP180
  DS18B20_Waterproof = DS18B20 1-Wire Temperature Sensor Probe Cable

nets:
  VDD: DHT22.VDD, part_2.Pin_1, DS18B20_Waterproof.VDD
  N1: DHT22.DATA, part.Pin_0
  GND: DHT22.GND, part_4.Pin_1, BMP180.GND, DS18B20_Waterproof.GND
  N2: part_2.Pin_0, DS18B20_Waterproof.shield
  N3: part_3.Pin_1, part_4.Pin_0

notes:
  WeMos Outside Box:
  - mesure de la T° via DS18B20 (?waterproof ou non vu que le DHT22 ne l'est pas?) sur D4
  - mesure du % d'humidité via DHT22 (module) sur D3
  - utilisation du deep sleep entre 2 mesures (shunt RST -- D0)
  Optionnel:
  - mesure de la pression atmosphérique via BMP180 sur D1-D2 (I2C)
  - mesure de la tension via A0 (et pont diviseur)
  Alimentation:
  - via adaptateur/chargeur 220V to 5V (1A) et connecteur Micro-USB
  - prévoir long cable USB (2m)
  A connecter au '+' de la batterie
  Attention de pas oublier de connecter le GND (-) de la batterie au GND du WeMos !!

custom parts:
  Adafruit BMP180: This precision sensor from Bosch is the best low-cost sensing solution for measuring barometric pressure and temperature. Because pressure changes with altitude you can also use it as an altimeter! The sensor is soldered onto a PCB with a 3.3V regulator, I2C level shifter and pull-up resistors on the I2C pins. The BMP180 is the next-generation of sensors from Bosch, and replaces the BMP085.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
